# Fritzing sketch Schematic (saved by Fritzing 1.0.2b)

parts:
  U1 = ESP32-38PinWide [part_number=ESP32-38PinWide]
  Part1 = RFID-RC522-v3

nets:
  N1: U1.3.3, Part1.3.3V
  N2: U1.GPIO32, Part1.RST
  N3: U1.GPIO33, Part1.SDA
  GND: U1.GND, Part1.GND
  N4: U1.GPIO18, Part1.SCK
  N5: U1.GPIO19, Part1.MISO
  N6: U1.GPIO23, Part1.MOSI

custom parts:
  ESP32-38PinWide: Generic 38-Pin ESP32 with wide format (only access to one side of pins on a breadboard) based on Stephen Lilley's HiLetgo ESP-WROOM-32 ESP32 ESP-32S Development Board.
  RFID-RC522-v3: A simple China made RFID-RC522 Reader (6x4 cm); do check the pin labels, as this is a MFRC522 based clone.
